# Fritzing sketch PIR (saved by Fritzing 0.9.3b)
breadboards: 1

parts:
  Part1 = HC-SR501 Body Sensor Module
  Part2 = Arduino Uno (Rev3)

nets:
  VCC: Part1.VCC, Part2.5V
  N1: Part1.OUT, Part2.D7
  GND: Part1.GND, Part2.GND

custom parts:
  HC-SR501 Body Sensor Module: Pyroelectric Infrared PIR Motion Sensor Detector Module
